// Logisim project Manas-CPU.circ as structural Verilog: 2 circuits, main circuit main
module main (
);

  wire and_1_out, and_2_out, and_3_out, and_4_out, Check_EndPrg, Clear_Btn, CLK, clock_1_out,
       controlled_buffer_5_out, Copy_Prg_ROM, EI, Enable_Prg_Counter, End_Prg, EO, Inv_Clock, JZ,
       Micro_ovrflw, MU, not_1_out, not_3_out, not_4_out, or_1_out, or_3_out, or_4_out, Prg_end_clear,
       Read_Ins_Reg, Read_Mem, Read_Prg_Counter, Read_Reg_A, Read_Reg_B, Read_Reg_C, SL, SR, Stop_Clock, SU,
       Write_Addr_Reg, Write_Ins_Reg, Write_Mem, Write_Prg_Counter, Write_Reg_A, Write_Reg_B, Write_Reg_C,
       ZF, ZF_In;
  wire [2:0] dipswitch_1_sw3, Microinstruction_Counter_q;
  wire [4:0] Instruction_Decoder, register_1_q;
  wire [10:0] Instruction_Register_q;
  wire [12:3] Microprogram_ROM_data;
  wire [15:0] Addr_Bus, alu_1_result_out, ALU_In_A, ALU_In_B, controlled_buffer_8_out, Data_Bus, Memory_dout,
       Prg_Counter, Program_ROM_data, Register_C_q;

  Clock clock_1 (.out(clock_1_out));
  not not_1 (not_1_out, Stop_Clock);
  assign CLK = not_1_out ? clock_1_out : 1'bz;  // Controlled_Buffer controlled_buffer_1
  not not_2 (Inv_Clock, CLK);
  Register #(.trigger("high"), .width(1)) Zero_Flag_Register (.D(ZF_In), .en(EO), .clk(CLK), .Q(ZF));  // open: clr
  Register #(.trigger("high"), .width(16)) Register_A (
    .D(Data_Bus), .en(Write_Reg_A), .clk(CLK), .Q(ALU_In_A));  // open: clr
  Register #(.trigger("high"), .width(16)) Register_B (
    .D(Data_Bus), .en(Write_Reg_B), .clk(CLK), .Q(ALU_In_B));  // open: clr
  Register #(.trigger("high"), .width(16)) Register_C (
    .D(Data_Bus), .en(Write_Reg_C), .clk(CLK), .Q(Register_C_q));  // open: clr
  // Probe on Data_Bus
  assign Data_Bus = Read_Reg_A ? ALU_In_A : 16'bz;  // Controlled_Buffer controlled_buffer_2
  assign Data_Bus = Read_Reg_B ? ALU_In_B : 16'bz;  // Controlled_Buffer controlled_buffer_3
  assign Data_Bus = Read_Reg_C ? Register_C_q : 16'bz;  // Controlled_Buffer controlled_buffer_4
  or or_1 (or_1_out, Clear_Btn, controlled_buffer_5_out);
  assign controlled_buffer_5_out = not_3_out ? EI : 1'bz;  // Controlled_Buffer controlled_buffer_5
  not not_3 (not_3_out, Inv_Clock);
  and and_1 (and_1_out, Check_EndPrg, End_Prg);
  or or_2 (Prg_end_clear, Clear_Btn, and_1_out);
  Counter #(.max('h7), .width(3)) Microinstruction_Counter (
    .clr(or_1_out), .load(and_1_out), .clk(Inv_Clock), .D(3'b100), .carry(Micro_ovrflw),
    .Q(Microinstruction_Counter_q));  // open: up, count
  Button button_1 (.out(Clear_Btn));
  DipSwitch #(.number(3)) dipswitch_1 (.sw1(dipswitch_1_sw3[2]), .sw2(dipswitch_1_sw3[1]), .sw3(dipswitch_1_sw3[0]));
  Register #(.trigger("high"), .width(5)) register_1 (
    .D(Instruction_Decoder), .en(or_3_out), .clk(CLK), .Q(register_1_q));  // open: clr
  or or_3 (or_3_out, EI, Micro_ovrflw);
  // Probe on {register_1_q, Microinstruction_Counter_q}
  ROM #(.dataWidth(16)) Microprogram_ROM (
    .addr({register_1_q, Microinstruction_Counter_q}),
    .data({Copy_Prg_ROM, Check_EndPrg, JZ, Microprogram_ROM_data[12:10], EO, Microprogram_ROM_data[8:3], Enable_Prg_Counter, EI, Stop_Clock}));
  Register #(.trigger("falling"), .width(16)) Instruction_Register (
    .D(Data_Bus), .en(Write_Ins_Reg), .clk(CLK), .Q({Instruction_Decoder, Instruction_Register_q}),
    .clr(Clear_Btn));
  // Probe on {Instruction_Decoder, Instruction_Register_q}
  ALU alu_1 (
    .A(ALU_In_A), .B(ALU_In_B), .EO(EO), .Sub(SU), .Mult(MU), .BShL(SL), .BShR(SR), .CLK(CLK),
    .Result_Out(alu_1_result_out), .Zero_Flag(ZF_In));
  // Probe on {Copy_Prg_ROM, Check_EndPrg, JZ, Microprogram_ROM_data[12:10], EO, Microprogram_ROM_data[8:3], Enable_Prg_Counter, EI, Stop_Clock}
  // Probe on {Copy_Prg_ROM, Check_EndPrg, JZ, Microprogram_ROM_data[12:10], EO, Microprogram_ROM_data[8:3], Enable_Prg_Counter, EI, Stop_Clock}
  and and_2 (and_2_out, ~Write_Ins_Reg, Read_Ins_Reg);  // AND_Gate
  // Probe on Instruction_Decoder
  assign Data_Bus = EO ? alu_1_result_out : 16'bz;  // Controlled_Buffer controlled_buffer_6
  // Probe on alu_1_result_out
  // Probe on Data_Bus
  assign Data_Bus = and_2_out ? {{5{1'b0}}, Instruction_Register_q} : 16'bz;  // Controlled_Buffer controlled_buffer_7
  Demultiplexer #(.select(3)) demultiplexer_1 (
    .out1(SU), .out2(MU), .out3(SL), .out4(SR), .in(1'b1), .sel(Microprogram_ROM_data[12:10]));  // open: out0, out5, out6, out7
  // Probe on Microprogram_ROM_data[12:10]
  Demultiplexer #(.select(3)) demultiplexer_2 (
    .out1(Read_Reg_A), .out2(Read_Reg_B), .out3(Read_Reg_C), .out4(Read_Mem), .out5(Read_Ins_Reg),
    .out6(Read_Prg_Counter), .in(1'b1), .sel(Microprogram_ROM_data[8:6]));  // open: out0, out7
  // Probe on Microprogram_ROM_data[8:6]
  Demultiplexer #(.select(3)) demultiplexer_3 (
    .out1(Write_Reg_A), .out2(Write_Reg_B), .out3(Write_Reg_C), .out4(Write_Mem), .out5(Write_Addr_Reg),
    .out6(Write_Ins_Reg), .out7(Write_Prg_Counter), .in(1'b1), .sel(Microprogram_ROM_data[5:3]));  // open: out0
  // Probe on Microprogram_ROM_data[5:3]
  not not_4 (not_4_out, Copy_Prg_ROM);
  Register #(.trigger("falling"), .width(16)) Mem_Address_Register (
    .D(controlled_buffer_8_out), .en(Write_Addr_Reg), .clk(CLK), .Q(Addr_Bus), .clr(Prg_end_clear));
  assign controlled_buffer_8_out = not_4_out ? Data_Bus : 16'bz;  // Controlled_Buffer controlled_buffer_8
  assign controlled_buffer_8_out = Copy_Prg_ROM ? Prg_Counter : 16'bz;  // Controlled_Buffer controlled_buffer_9
  and and_3 (and_3_out, ZF, JZ);
  RAM #(.addrWidth(16), .dataWidth(16)) Memory (
    .addr(Addr_Bus), .we(Write_Mem), .oe(Read_Mem), .clk(CLK), .din(Data_Bus), .dout(Memory_dout));
  or or_4 (or_4_out, and_3_out, Write_Prg_Counter);
  assign Data_Bus = Read_Mem ? Memory_dout : 16'bz;  // Controlled_Buffer controlled_buffer_10
  Counter #(.max('hffff), .width(16)) Program_Counter (
    .clr(Prg_end_clear), .load(or_4_out), .count(Enable_Prg_Counter), .clk(CLK), .D(Data_Bus), .Q(Prg_Counter));  // open: up, carry
  ROM #(.addrWidth(16), .dataWidth(16)) Program_ROM (.addr(Addr_Bus), .data(Program_ROM_data));
  assign Data_Bus = Read_Prg_Counter ? Prg_Counter : 16'bz;  // Controlled_Buffer controlled_buffer_11
  and and_4 (and_4_out, Program_ROM_data[15], Program_ROM_data[14], Program_ROM_data[13], Program_ROM_data[12], Program_ROM_data[11]);
  assign Data_Bus = Copy_Prg_ROM ? Program_ROM_data : 16'bz;  // Controlled_Buffer controlled_buffer_12
  T_Flip_Flop t_ff_1 (.T(and_4_out), .clk(and_4_out), .Q(End_Prg));  // open: Qn, reset, preset

  // Notes on the sheet:
  //   Clock
  //   General registers
  //   contents of Microprogram_ROM (hex, n*v repeats v):
  //   8028 c000 8024 2 1a8 134 2 0 168 108 1a8 134 2 0 0 0 168 110 1a8 134 2 0 0 0 168 118 1a8 134 2 0 0 0
  //   148 1a8 134 2 4*0 150 1a8 134 2 4*0 158 1a8 134 2 4*0 168 60 1a8 134 2 0 0 0 168 a0 1a8 134 2 0 0 0
  //   168 e0 1a8 134 2 0 0 0 208 1a8 134 2 4*0 608 1a8 134 2 4*0 a08 1a8 134 2 4*0 e08 1a8 134 2 4*0 1208
  //   1a8 134 2 4*0 140 178 1a8 134 2 0 0 0 140 2140 1a8 134 2 0 0 0 68 108 1a8 134 2 0 0 0 68 a0 1a8 134
  //   2 0 0 0 58 88 d0 1a8 134 2 0 0 50 c8 98 1a8 134 2 0 0 1 1a8 134 2 4*0 1a8 134 2
  //   ALU
  //   Read lowest 11-bits if Read enabled and Write not enabled
  //   RAM
  //   contents of Program_ROM (hex, n*v repeats v):
  //   805 2801 5800 8006 7802 a a800 f800
endmodule

module ALU (
  input  [15:0] A,
  input  [15:0] B,
  input  EO,
  input  Sub,
  input  Mult,
  input  BShL,
  input  BShR,
  input  CLK,
  output [15:0] Result_Out,
  output Zero_Flag
);

  wire not_1_out, not_2_out, or_2_out, Shift;
  wire [15:0] A_t, adder_1_out, B_t, controlled_buffer_2_out, controlled_inverter_1_out, multiplier_1_out,
       shifter_1_out, shifter_2_out;

  Register #(.width(16)) register_1 (.D(A), .en(EO), .clk(EO), .Q(A_t));  // open: clr
  Register #(.width(16)) register_2 (.D(B), .en(EO), .clk(EO), .Q(B_t));  // open: clr
  or or_1 (Shift, BShL, BShR);
  assign controlled_inverter_1_out = Sub ? ~B_t : 16'bz;  // Controlled_Inverter controlled_inverter_1
  assign controlled_inverter_1_out = not_1_out ? B_t : 16'bz;  // Controlled_Buffer controlled_buffer_1
  not not_1 (not_1_out, Sub);
  Multiplier #(.width(16)) multiplier_1 (.a(A_t), .b(B_t), .out(multiplier_1_out));  // open: cin, cout
  Shifter #(.width(16)) shifter_1 (.in(A_t), .\dist (B_t[3:0]), .out(shifter_1_out));
  Shifter #(.shift("lr"), .width(16)) shifter_2 (.in(A_t), .\dist (B_t[3:0]), .out(shifter_2_out));
  Adder #(.width(16)) adder_1 (.a(A_t), .b(controlled_inverter_1_out), .out(adder_1_out), .cin(Sub));  // open: cout
  assign controlled_buffer_2_out = BShL ? shifter_1_out : 16'bz;  // Controlled_Buffer controlled_buffer_2
  assign controlled_buffer_2_out = BShR ? shifter_2_out : 16'bz;  // Controlled_Buffer controlled_buffer_3
  Multiplexer #(.select(2), .width(16)) multiplexer_1 (
    .in0(adder_1_out), .in1(multiplier_1_out), .in3(controlled_buffer_2_out), .out(Result_Out),
    .sel({Shift, Mult}));  // open: in2
  // Probe on Result_Out
  // Probe on Result_Out
  or or_2 (or_2_out, Result_Out[15], Result_Out[14], Result_Out[13], Result_Out[12], Result_Out[11], Result_Out[10], Result_Out[9], Result_Out[8], Result_Out[7], Result_Out[6], Result_Out[5], Result_Out[4], Result_Out[3], Result_Out[2], Result_Out[1], Result_Out[0]);
  not not_2 (not_2_out, or_2_out);
  assign Zero_Flag = EO ? not_2_out : 1'bz;  // Controlled_Buffer controlled_buffer_4

  // Other names for the same wires on the sheet: MU = Mult; SL = BShL; SR = BShR; SU = Sub

  // Notes on the sheet:
  //   Input A
  //   Input B
  //   If EO enable a specified operation, or addition if not specified, using A and B
  //   First 4 bits of B to decide amount of shifts
  //   Operation Inputs
  //   Check each bit if any are 1 and invert result
endmodule
